# Fritzing sketch RA1_Amp (saved by Fritzing 0.9.0b)
perfboards: 1

parts:
  J1 = rounded female pin header, 5 pins [form="♀ (female rounded)"]
  C1 = Electrolytic Capacitor [capacitance=5µF voltage=50V package="200 mil [THT, electrolytic]"]
  C2 = Electrolytic Capacitor [capacitance=5µF voltage=50V package="200 mil [THT, electrolytic]"]
  R2 = Resistor [tolerance=±1% resistance=121k package=THT]
  R4 = Resistor [tolerance=±1% resistance=121k package=THT]
  R6 = Resistor [tolerance=±1% resistance=464 package=THT]
  R7 = Resistor [tolerance=±1% resistance=464 package=THT]
  R1 = Rotary Potentiometer (Large) [maximum_resistance=100kΩ package=THT]
  R8 = Resistor [tolerance=±1% resistance=100k package=THT]  # not connected
  R9 = Resistor [tolerance=±1% resistance=100k package=THT]
  J3 = rounded female pin header, 5 pins [form="♀ (female rounded)"]
  J1_2 = rounded female pin header, 7 pins [form="♀ (female rounded)"]
  J4 = rounded female pin header, 7 pins [form="♀ (female rounded)"]
  U3 = LM 358 Dual Op-Amp [package="DIP8 [THT]"]

nets:
  N1: J1.pin1, R2.Pin_0, J1_2.pin1
  N2: J1.pin5, J1_2.pin7
  N3: C1.+, R9.Pin_1, U3.connector2
  N4: C2.-, U3.connector4
  N5: C2.+, R1.wiper
  N6: R2.Pin_1, R6.Pin_1
  N7: R4.Pin_1, R7.Pin_1, U3.connector1
  N8: R7.Pin_0, J4.pin7
  N9: R1.leg1, J1_2.pin5
  N10: J3.pin1, U3.connector7
  N11: J3.pin3, J4.pin1
  N12: J3.pin5, U3.connector3
  N13: J1_2.pin3, J4.pin3
  N14: J4.pin5, U3.connector6

notes:
  -Vcc GND +Vcc
  Left Right Mic Gnd
  Right Left
  In   Out  Gnd
  Left
  Right
  OPA
  464R
  121K
  100K
