# Fritzing sketch RA1_Power (saved by Fritzing 0.9.0b)
perfboards: 1

parts:
  J2 = female pin header, 5 pins [form="♀ (female)"]
  U3 = 555 Timer [package="DIP8 [THT]"]
  D5 = Schottky Diode [part_number=1N5817 package="300 mil [THT]"]
  D6 = Rectifier Diode [part_number=1N4001 package="300 mil [THT]"]
  S3 = Pushbutton [package=THT]
  Power_plug3 = Power plug
  LED4 = LED - 5mm [color="Blue (525nm)" package="5 mm [THT]"]
  LED5 = LED - 5mm [color="Blue (525nm)" package="5 mm [THT]"]
  R8 = Resistor [tolerance=±1% resistance=12k package=THT]
  R9 = Resistor [tolerance=±1% resistance=464 package=THT]
  C13 = Electrolytic Capacitor [capacitance=22µF voltage=50V package="100 mil [THT, electrolytic]"]
  C14 = Electrolytic Capacitor [capacitance=22µF voltage=50V package="100 mil [THT, electrolytic]"]
  J3 = female pin header, 3 pins [form="♀ (female)"]
  C15 = Ceramic Capacitor [capacitance=0.01µF voltage=35V package="100 mil [THT, multilayer]"]
  C16 = Tantalum Capacitor [capacitance=2nF voltage=35V package="100 mil [THT, tantalum]"]

nets:
  N1: J2.pin1, D5.anode
  N2: J2.pin3, U3.Output, R8.Pin_1, C13.-, C14.+
  N3: J2.pin5, D6.cathode
  N4: U3.Trigger, U3.Threshold, C16.-
  N5: U3.Vcc_Supply_Voltage, C15.1
  N6: D5.cathode, Power_plug3.GND, J3.pin1
  N7: D6.anode, S3.leg0, J3.pin3
  N8: S3.leg1, Power_plug3.VCC
  N9: LED4.cathode, R9.Pin_1
  N10: LED4.anode, LED5.cathode

notes:
  DC +
  DC -
  0.01uF
  2000pF
  - 22uF +
  464R
  12K
  1N5821
  NE555
  -Vcc GND +Vcc
  22uF
  +Vcc GND -Vcc
  -  +
